# Fritzing sketch Aoi_circuit (saved by Fritzing 0.9.2b)
breadboards: 1

parts:
  NOT = IC, DIP package, 14 pins [chip_label=74LS04N part_number=NOT]
  AND = IC, DIP package, 14 pins [chip_label=74LS08N]
  OR = IC, DIP package, 14 pins [chip_label=74LS32N]
  LED1 = LED - 5mm [color="Red (633nm)" package="5 mm [THT]"]
  R1 = Resistor [tolerance=±5% resistance=220 package=THT]

nets:
  N1: NOT.pin1, AND.pin1, AND.pin9
  N2: NOT.pin2, AND.pin4
  N3: NOT.pin3, AND.pin5, AND.pin13
  N4: NOT.pin4, AND.pin2
  N5: NOT.pin6, AND.pin10
  N6: NOT.pin7, AND.pin7, OR.pin7, R1.Pin_1
  N7: NOT.pin14, AND.pin14, OR.pin14
  N8: AND.pin3, OR.pin1
  N9: AND.pin6, OR.pin2
  N10: AND.pin8, AND.pin12
  N11: AND.pin11, OR.pin5
  N12: OR.pin3, OR.pin4
  N13: OR.pin6, LED1.anode
  N14: LED1.cathode, R1.Pin_0

notes:
  A
  C
  B
